# Fritzing sketch Smart-room-controller (saved by Fritzing 0.9.4)
breadboards: 1

parts:
  Part1 = HC-SR501 Body Sensor Module
  WIZ820io1 = WIZ820io [part_number=WIZ820io]
  OLED_I2C1 = OLED 128x64 I2C Monochrome Display
  Part3 = BME280 Breakout
  S2 = Pushbutton [package="[THT]"]
  Teensy_3_1 = Teensy 3.1
  R1 = 220 Ω Resistor [package="0603 [SMD]"]

nets:
  VCC: Part1.VCC, OLED_I2C1.VDD, Part3.3.3V, S2.Pin_3, S2.Pin_4, R1.Pin_0
  GND: Part1.GND, WIZ820io1.GND, OLED_I2C1.GND, Part3.GND, Teensy_3_1.GND, R1.Pin_1
  N1: OLED_I2C1.SDA, Part3.SDI/SDA
  N2: OLED_I2C1.SCK, Part3.SCK/SCL
  N3: S2.Pin_1, S2.Pin_2

custom parts:
  HC-SR501 Body Sensor Module: Pyroelectric Infrared PIR Motion Sensor Detector Module
  Pushbutton: A generic pushbutton.
  220 Ω Resistor: A generic resistor (0.25W)
